# Fritzing sketch 19p (saved by Fritzing 0.9.2b)
breadboards: 1

parts:
  Raspberry_Pi1 = Raspberry Pi 2
  R2 = Resistor [tolerance=±5% resistance=10k package=THT]
  S1 = Pushbutton [package=THT]
  LED1 = LED - 5mm [color="Red (633nm)" package="5 mm [THT]"]
  R1 = Resistor [tolerance=±5% resistance=1k package=THT]

nets:
  3V3: Raspberry_Pi1.3v3, Raspberry_Pi1.3V3, S1.leg1
  N1: Raspberry_Pi1.GPIO25, LED1.anode
  N2: Raspberry_Pi1.GPIO24, R2.Pin_0, S1.leg0
  N3: Raspberry_Pi1.GND, R2.Pin_1, R1.Pin_1
  N4: LED1.cathode, R1.Pin_0
