# Fritzing sketch 23p (saved by Fritzing 0.9.2b)
breadboards: 1

parts:
  Raspberry_Pi1 = Raspberry Pi 2
  R1 = Resistor [tolerance=±5% resistance=330 package=THT]
  R2 = Resistor [tolerance=±5% resistance=330 package=THT]
  R3 = Resistor [tolerance=±5% resistance=330 package=THT]
  LED1 = RGB LED (com. cathode, rgb) [package="5 mm [THT]"]

nets:
  N1: Raspberry_Pi1.GPIO22, R1.Pin_1
  N2: Raspberry_Pi1.3V3, LED1.common_cathode
  N3: Raspberry_Pi1.GPIO7, R3.Pin_1
  N4: Raspberry_Pi1.GPIO23, R2.Pin_1
  N5: R1.Pin_0, LED1.red_anode
  N6: R2.Pin_0, LED1.blue_anode
  N7: R3.Pin_0, LED1.green_anode
