# Fritzing sketch 29p_motor (saved by Fritzing 0.9.2b)
breadboards: 1

parts:
  Raspberry_Pi1 = Raspberry Pi 2
  VCC1 = Battery
  R1 = Resistor [tolerance=±5% resistance=220 package=THT]
  M1 = DC Motor
  IC1 = IC, DIP package, 20 pins [chip_label=TA7291P]

nets:
  N1: Raspberry_Pi1.GPIO17, IC1.pin5
  N2: Raspberry_Pi1.GPIO27, IC1.pin6
  N3: Raspberry_Pi1.GND, VCC1.-, IC1.pin1
  N4: Raspberry_Pi1.5V, IC1.pin7
  N5: VCC1.+, R1.Pin_1, IC1.pin8
  N6: R1.Pin_0, IC1.pin4
  N7: M1.pin_1, IC1.pin2
  N8: M1.pin_2, IC1.pin10
