# Fritzing sketch 7seg4 (saved by Fritzing 0.9.2b)
breadboards: 1

parts:
  Raspberry_Pi1 = Raspberry Pi 2
  R2 = Resistor [tolerance=±5% resistance=1k package=THT]
  R3 = Resistor [tolerance=±5% resistance=1k package=THT]
  R4 = Resistor [tolerance=±5% resistance=1k package=THT]
  U1 = 7-SEGMENT-4DIGIT [package=7-segment-4digit]
  R5 = Resistor [tolerance=±5% resistance=1k package=THT]
  R6 = Resistor [tolerance=±5% resistance=1k package=THT]
  R7 = Resistor [tolerance=±5% resistance=1k package=THT]
  R8 = Resistor [tolerance=±5% resistance=1k package=THT]
  R9 = Resistor [tolerance=±5% resistance=1k package=THT]

nets:
  N1: Raspberry_Pi1.GPIO2, Raspberry_Pi1.GPIO17, R3.Pin_0
  N2: Raspberry_Pi1.GPIO4, R2.Pin_0
  N3: Raspberry_Pi1.GPIO27, R4.Pin_0
  N4: Raspberry_Pi1.GPIO22, R5.Pin_0
  N5: Raspberry_Pi1.GPIO21, U1.16
  N6: Raspberry_Pi1.GPIO20, U1.13
  N7: Raspberry_Pi1.GPIO16, U1.11
  N8: Raspberry_Pi1.GPIO12, U1.6
  N9: Raspberry_Pi1.GND, Raspberry_Pi1.GPIO25, R7.Pin_0
  N10: Raspberry_Pi1.GPIO7, R8.Pin_0
  N11: Raspberry_Pi1.GPIO24, Raspberry_Pi1.GPIO15, R9.Pin_0
  N12: Raspberry_Pi1.GPIO23, R6.Pin_0
  N13: R2.Pin_1, U1.15
  N14: R3.Pin_1, U1.9
  N15: R4.Pin_1, U1.4
  N16: U1.1, R6.Pin_1
  N17: U1.2, R5.Pin_1
  N18: U1.3, R8.Pin_1
  N19: U1.5, R7.Pin_1
  N20: U1.14, R9.Pin_1
