# Fritzing sketch 7seg4digitcathod (saved by Fritzing 0.9.2b)
breadboards: 1

parts:
  Raspberry_Pi1 = Raspberry Pi 2
  U1 = 7-SEGMENT-4DIGIT [package=7-segment-4digit]
  R1 = Resistor [tolerance=±5% resistance=220 package=THT]
  R2 = Resistor [tolerance=±5% resistance=220 package=THT]
  R3 = Resistor [tolerance=±5% resistance=220 package=THT]
  R4 = Resistor [tolerance=±5% resistance=220 package=THT]

nets:
  N1: Raspberry_Pi1.GPIO4, U1.15
  N2: Raspberry_Pi1.GND, Raspberry_Pi1.GPIO7, Raspberry_Pi1.GPIO15, U1.3, R2.Pin_0
  N3: Raspberry_Pi1.GPIO17, U1.9
  N4: Raspberry_Pi1.GPIO27, U1.4
  N5: Raspberry_Pi1.GPIO22, U1.2
  N6: Raspberry_Pi1.GPIO10, U1.1
  N7: Raspberry_Pi1.GPIO9, U1.14
  N8: Raspberry_Pi1.GPIO11, U1.5
  N9: Raspberry_Pi1.GPIO23, R4.Pin_0
  N10: Raspberry_Pi1.GPIO18, R3.Pin_0
  N11: Raspberry_Pi1.GPIO14, R1.Pin_0
  N12: U1.6, R4.Pin_1
  N13: U1.11, R3.Pin_1
  N14: U1.13, R2.Pin_1
  N15: U1.16, R1.Pin_1
