# Fritzing sketch 24p (saved by Fritzing 0.9.2b)
breadboards: 1

parts:
  Raspberry_Pi1 = Raspberry Pi 2
  7_Segment1 = 7 Segment Display

nets:
  N1: Raspberry_Pi1.GPIO4, 7_Segment1.Segment_D
  N2: Raspberry_Pi1.GPIO17, 7_Segment1.Segment_E
  N3: Raspberry_Pi1.GPIO27, 7_Segment1.Segment_F
  N4: Raspberry_Pi1.GPIO22, 7_Segment1.Segment_A
  N5: Raspberry_Pi1.GPIO7, 7_Segment1.Segment_DP
  N6: Raspberry_Pi1.GPIO25, 7_Segment1.Segment_G
  N7: Raspberry_Pi1.GPIO24, 7_Segment1.Segment_C
  N8: Raspberry_Pi1.GPIO23, 7_Segment1.Segment_B
  N9: Raspberry_Pi1.GND, 7_Segment1.common_anode
