# Fritzing sketch 25p (saved by Fritzing 0.9.2b)
breadboards: 1

parts:
  Raspberry_Pi1 = Raspberry Pi 2
  R1 = Resistor [tolerance=±5% resistance=150 package=THT]
  LED1 = LED - 5mm [color="Red (633nm)" package="5 mm [THT]"]
  R2 = Resistor [tolerance=±5% resistance=10k package=THT]
  Q1 = NPN-Transistor [package="TO92 [THT]"]

nets:
  N1: Raspberry_Pi1.GPIO4, R2.Pin_0
  N2: Raspberry_Pi1.GND, Q1.E
  N3: Raspberry_Pi1.5V, R1.Pin_1
  N4: R1.Pin_0, LED1.anode
  N5: LED1.cathode, Q1.C
  N6: R2.Pin_1, Q1.B
