# Fritzing sketch 28p (saved by Fritzing 0.9.2b)
breadboards: 1

parts:
  Raspberry_Pi1 = Raspberry Pi 2
  SPKR1 = Loudspeaker

nets:
  N1: Raspberry_Pi1.GND, SPKR1.pin2
  N2: Raspberry_Pi1.GPIO25, SPKR1.pin1
