# Fritzing sketch 29p (saved by Fritzing 0.9.2b)
breadboards: 1

parts:
  Raspberry_Pi1 = Raspberry Pi 2
  M1 = DC Motor
  VCC1 = 4 x AAA Battery Mount
  U1 = TA7291P [package=HSIP10-P-2.54(THT)]
  R1 = Resistor [tolerance=±5% resistance=220 package=THT]

nets:
  N1: Raspberry_Pi1.GPIO17, U1.IN1
  N2: Raspberry_Pi1.GPIO27, U1.IN2
  GND: Raspberry_Pi1.GND, VCC1.-, U1.GND
  5V: Raspberry_Pi1.5V, U1.Vcc
  N3: M1.pin_1, U1.OUT2
  N4: M1.pin_2, U1.OUT1
  N5: VCC1.+, U1.Vs, R1.Pin_1
  N6: U1.Vref, R1.Pin_0

custom parts:
  TA7291P: The IC are Full-Bridge Driver. 4 modes available (CW / CCW / STOP / BRAKE) and PWM control. Output current:1.0 A (AVE.) 2.0 A (PEAK)
