# Fritzing sketch 31p (saved by Fritzing 0.9.2b)
breadboards: 1

parts:
  Raspberry_Pi1 = Raspberry Pi 2
  GLCD_128x1 = 128 x 64 Graphic LCD
  R1 = Resistor [tolerance=±5% resistance=10k package=THT]
  R3 = Trimmer Potentiometer [maximum_resistance=10kΩ package=THT]
  C1 = Capacitor [package=cap-pth-small-kit]

nets:
  3V3: Raspberry_Pi1.3v3, Raspberry_Pi1.3V3, Raspberry_Pi1.GPIO24, Raspberry_Pi1.5V, GLCD_128x1.2_Vdd, GLCD_128x1.14_DB7, GLCD_128x1.19_A(+), R1.Pin_0, R3.leg2
  N1: Raspberry_Pi1.GPIO3, Raspberry_Pi1.GND, Raspberry_Pi1.GPIO7, GLCD_128x1.1_Vss, GLCD_128x1.5_R/W, GLCD_128x1.7_DB0, GLCD_128x1.20_K(-), C1.2
  N2: Raspberry_Pi1.GPIO4, Raspberry_Pi1.GPIO14, GLCD_128x1.4_D/I
  N3: Raspberry_Pi1.GPIO17, GLCD_128x1.15_CS1
  N4: Raspberry_Pi1.GPIO22, GLCD_128x1.12_DB5
  N5: Raspberry_Pi1.GPIO10, GLCD_128x1.10_DB3
  N6: Raspberry_Pi1.GPIO9, GLCD_128x1.9_BD2
  N7: Raspberry_Pi1.GPIO11, GLCD_128x1.11_DB4
  N8: Raspberry_Pi1.GPIO8, Raspberry_Pi1.GPIO25, GLCD_128x1.8_DB1
  N9: Raspberry_Pi1.GPIO23, GLCD_128x1.13_DB6
  N10: Raspberry_Pi1.GPIO18, GLCD_128x1.16_CS2
  N11: Raspberry_Pi1.GPIO15, GLCD_128x1.6_Enable
  N12: GLCD_128x1.3_Vo, R3.wiper
  N13: GLCD_128x1.17_RST, R1.Pin_1, C1.1
  N14: GLCD_128x1.18_Vout, R3.leg1
