# Fritzing sketch 33p (saved by Fritzing 0.9.2b)
breadboards: 1

parts:
  Raspberry_Pi1 = Raspberry Pi 2
  T1 = LM35 Temperature Sensor [package="TO92 [THT]"]
  IC1 = IC, DIP package, 8 pins [chip_label=MCP3002]
  R2 = Trimmer Potentiometer [maximum_resistance=10kΩ package=THT]

nets:
  3V3: Raspberry_Pi1.3v3, Raspberry_Pi1.3V3, IC1.pin8
  N1: Raspberry_Pi1.GPIO10, IC1.pin5
  N2: Raspberry_Pi1.GPIO9, IC1.pin6
  N3: Raspberry_Pi1.GPIO11, IC1.pin7
  GND: Raspberry_Pi1.GND, T1.GND, IC1.pin4, R2.leg2
  N4: Raspberry_Pi1.GPIO8, IC1.pin1
  N5: Raspberry_Pi1.5V, T1.+Vs, R2.leg1
  N6: T1.Vout, IC1.pin3
  N7: IC1.pin2, R2.wiper
