# Fritzing sketch 温度計 (saved by Fritzing 0.9.2b)
breadboards: 1

parts:
  Raspberry_Pi1 = Raspberry Pi 2
  T1 = LM35 Temperature Sensor [package="TO92 [THT]"]
  IC1 = IC, DIP package, 8 pins [chip_label=MCP3002]
  R1 = Resistor [tolerance=±5% resistance=1k package=THT]
  R2 = Resistor [tolerance=±5% resistance=1k package=THT]
  R3 = Resistor [tolerance=±5% resistance=1k package=THT]
  R4 = Resistor [tolerance=±5% resistance=1k package=THT]
  R5 = Resistor [tolerance=±5% resistance=1k package=THT]
  R6 = Resistor [tolerance=±5% resistance=1k package=THT]
  R7 = Resistor [tolerance=±5% resistance=1k package=THT]
  R9 = Resistor [tolerance=±5% resistance=1k package=THT]
  R10 = Resistor [tolerance=±5% resistance=1k package=THT]
  R11 = Resistor [tolerance=±5% resistance=1k package=THT]
  R12 = Resistor [tolerance=±5% resistance=1k package=THT]
  R13 = Resistor [tolerance=±5% resistance=1k package=THT]
  R14 = Resistor [tolerance=±5% resistance=1k package=THT]
  R15 = Resistor [tolerance=±5% resistance=1k package=THT]
  7_Segment3 = 7 Segment Display
  7_Segment2 = 7 Segment Display

nets:
  3V3: Raspberry_Pi1.3v3, Raspberry_Pi1.3V3, IC1.pin8
  N1: Raspberry_Pi1.GPIO2, R1.Pin_1
  N2: Raspberry_Pi1.GPIO3, R3.Pin_1
  N3: Raspberry_Pi1.GPIO4, R5.Pin_1
  GND: Raspberry_Pi1.GND, T1.GND, IC1.pin2, IC1.pin4
  N4: Raspberry_Pi1.GPIO17, R7.Pin_1
  N5: Raspberry_Pi1.GPIO10, IC1.pin5
  N6: Raspberry_Pi1.GPIO9, IC1.pin6
  N7: Raspberry_Pi1.GPIO11, IC1.pin7
  N8: Raspberry_Pi1.GPIO6, R9.Pin_1
  N9: Raspberry_Pi1.GPIO13, R11.Pin_1
  N10: Raspberry_Pi1.GPIO19, R13.Pin_1
  N11: Raspberry_Pi1.GPIO26, R15.Pin_1
  N12: Raspberry_Pi1.GPIO21, R2.Pin_1
  N13: Raspberry_Pi1.GPIO20, R4.Pin_1
  N14: Raspberry_Pi1.GPIO16, R6.Pin_1
  N15: Raspberry_Pi1.GPIO8, IC1.pin1
  N16: Raspberry_Pi1.GPIO23, R10.Pin_1
  N17: Raspberry_Pi1.GPIO18, R12.Pin_1
  N18: Raspberry_Pi1.GPIO15, R14.Pin_1
  N19: Raspberry_Pi1.5V, T1.+Vs
  N20: T1.Vout, IC1.pin3
  N21: R1.Pin_0, 7_Segment2.Segment_A#10
  N22: R2.Pin_0, 7_Segment2.Segment_B
  N23: R3.Pin_0, 7_Segment2.Segment_C
  N24: R4.Pin_0, 7_Segment2.Segment_D
  N25: R5.Pin_0, 7_Segment2.Segment_E
  N26: R6.Pin_0, 7_Segment2.Segment_F
  N27: R7.Pin_0, 7_Segment2.Segment_A#1
  N28: R9.Pin_0, 7_Segment3.Segment_A#10
  N29: R10.Pin_0, 7_Segment3.Segment_B
  N30: R11.Pin_0, 7_Segment3.Segment_C
  N31: R12.Pin_0, 7_Segment3.Segment_D
  N32: R13.Pin_0, 7_Segment3.Segment_E
  N33: R14.Pin_0, 7_Segment3.Segment_F
  N34: R15.Pin_0, 7_Segment3.Segment_A#1
